# Fritzing sketch 紅外線溫度感測器 (saved by Fritzing 0.9.3b)
breadboards: 1

parts:
  元件1 = Arduino Uno (Rev3)
  SP1 = SPEAKER [package=pcb_mount_speaker]
  U1 = MLX90614 [package=to-39]
  PIR1 = PIR sensor
  DFRobot_DFPlayer_Mini1 = DFRobot DFPlayer Mini [part_number=DFR0299]
  Display1 = LCD screen 16x2 IIC [part_number=101290]
  R1 = Resistor [tolerance=±5% resistance=499k package=THT]

nets:
  N1: 元件1.A4/SDA, U1.PWM_SDA, Display1.SDA
  N2: 元件1.D8, DFRobot_DFPlayer_Mini1.TX
  N3: 元件1.D9_PWM, R1.Pin_0
  N4: 元件1.D10_PWM/SS, DFRobot_DFPlayer_Mini1.BUSY
  N5: 元件1.D13/SCK, PIR1.SIG
  N6: 元件1.A5/SCL, U1.SCL_VZ, Display1.SCL
  3V3: 元件1.3V3, U1.VDD
  VCC: 元件1.5V, PIR1.VDD, DFRobot_DFPlayer_Mini1.VCC, Display1.VCC
  GND: 元件1.GND, U1.VSS, PIR1.GND, DFRobot_DFPlayer_Mini1.GND-1, DFRobot_DFPlayer_Mini1.GND-2, Display1.GND
  N7: SP1.+, DFRobot_DFPlayer_Mini1.SPK_1
  N8: SP1.-, DFRobot_DFPlayer_Mini1.SPK_2
  N9: DFRobot_DFPlayer_Mini1.RX, R1.Pin_1

custom parts:
  LCD screen 16x2 IIC: LCD screen with HD44780 controller enables showing text, symbols, value or anything else that comes from Croduino/Arduino. It is capable of showing 16 symbols in two lines and therefore can be used in many projects that need to send clearly visible and legible output information.. • Color of symbols: White • Backlight: Blue • Dimensions: 80 x 36 x 12 mm • Screen dimensions: 64.5 x 16 mm •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
